// Logisim project 1 bit ALU block.circ as structural Verilog: 2 circuits, main circuit main
module main (
  input  [1:0] in_1,
  input  [1:0] in_2,
  input  in_3,
  input  in_4,
  input  [2:0] in_5,
  output [1:0] out_6,
  output out_7
);

  wire n1_bit_alu_1_out_7;

  _1_bit_alu u_1_bit_alu_1 (
    .out_6(out_6[0]), .Cin(in_3), .Sub(in_4), .B(in_1[0]), .A(in_2[0]), .out_7(n1_bit_alu_1_out_7),
    .Select_Bits_Op(in_5));
  _1_bit_alu u_1_bit_alu_2 (
    .out_6(out_6[1]), .Cin(n1_bit_alu_1_out_7), .Sub(in_4), .B(in_1[1]), .A(in_2[1]), .out_7(out_7),
    .Select_Bits_Op(in_5));
endmodule

module _1_bit_alu (
  input  Cin,
  input  Sub,
  input  B,
  input  A,
  input  [2:0] Select_Bits_Op,
  output out_6,
  output out_7
);

  wire adder_1_out, and_1_out, comparator_1_eq, comparator_1_gt, comparator_1_lt, multiplier_1_out, or_1_out,
       xor_1_out, xor_2_out;

  xor xor_1 (xor_1_out, B, Sub);
  and and_1 (and_1_out, A, B);
  or or_1 (or_1_out, A, B);
  xor xor_2 (xor_2_out, A, B);
  Adder #(.width(1)) adder_1 (.a(A), .b(xor_1_out), .out(adder_1_out), .cin(Cin), .cout(out_7));
  Multiplier #(.width(1)) multiplier_1 (.a(A), .b(B), .out(multiplier_1_out), .cin(Cin));  // open: cout
  Comparator #(.width(1)) comparator_1 (.a(A), .b(B), .gt(comparator_1_gt), .eq(comparator_1_eq), .lt(comparator_1_lt));
  Multiplexer #(.select(3), .enable("false")) multiplexer_1 (
    .in0(and_1_out), .in1(or_1_out), .in2(xor_2_out), .in3(adder_1_out), .in4(multiplier_1_out),
    .in5(comparator_1_gt), .in6(comparator_1_eq), .in7(comparator_1_lt), .out(out_6), .sel(Select_Bits_Op));
endmodule
