// Logisim project 16-bit_ALU.circ as structural Verilog: 2 circuits, main circuit main
module main (
  input  in_1,
  input  in_2,
  input  [15:0] in_3,
  input  [15:0] in_4,
  input  [2:0] in_5,
  output [15:0] out_6,
  output out_7
);

  wire n1_bit_alu_1_out_7, n1_bit_alu_2_out_7, n1_bit_alu_3_out_7, n1_bit_alu_4_out_7, n1_bit_alu_5_out_7,
       n1_bit_alu_6_out_7, n1_bit_alu_7_out_7, n1_bit_alu_8_out_7, n1_bit_alu_9_out_7, n1_bit_alu_10_out_7,
       n1_bit_alu_11_out_7, n1_bit_alu_12_out_7, n1_bit_alu_13_out_7, n1_bit_alu_14_out_7,
       n1_bit_alu_15_out_7;

  _1_bit_alu u_1_bit_alu_1 (
    .out_6(out_6[0]), .Cin(in_1), .Sub(in_2), .B(in_3[14]), .A(in_4[14]), .out_7(n1_bit_alu_1_out_7),
    .Select_Bits_Op(in_5));
  _1_bit_alu u_1_bit_alu_2 (
    .out_6(out_6[1]), .Cin(n1_bit_alu_1_out_7), .Sub(in_2), .B(in_3[15]), .A(in_4[15]),
    .out_7(n1_bit_alu_2_out_7), .Select_Bits_Op(in_5));
  _1_bit_alu u_1_bit_alu_3 (
    .out_6(out_6[2]), .Cin(n1_bit_alu_2_out_7), .Sub(in_2), .B(in_3[13]), .A(in_4[13]),
    .out_7(n1_bit_alu_3_out_7), .Select_Bits_Op(in_5));
  _1_bit_alu u_1_bit_alu_4 (
    .out_6(out_6[3]), .Cin(n1_bit_alu_3_out_7), .Sub(in_2), .B(in_3[12]), .A(in_4[12]),
    .out_7(n1_bit_alu_4_out_7), .Select_Bits_Op(in_5));
  _1_bit_alu u_1_bit_alu_5 (
    .out_6(out_6[4]), .Cin(n1_bit_alu_4_out_7), .Sub(in_2), .B(in_3[11]), .A(in_4[11]),
    .out_7(n1_bit_alu_5_out_7), .Select_Bits_Op(in_5));
  _1_bit_alu u_1_bit_alu_6 (
    .out_6(out_6[5]), .Cin(n1_bit_alu_5_out_7), .Sub(in_2), .B(in_3[10]), .A(in_4[10]),
    .out_7(n1_bit_alu_6_out_7), .Select_Bits_Op(in_5));
  _1_bit_alu u_1_bit_alu_7 (
    .out_6(out_6[6]), .Cin(n1_bit_alu_6_out_7), .Sub(in_2), .B(in_3[9]), .A(in_4[9]),
    .out_7(n1_bit_alu_7_out_7), .Select_Bits_Op(in_5));
  _1_bit_alu u_1_bit_alu_8 (
    .out_6(out_6[7]), .Cin(n1_bit_alu_7_out_7), .Sub(in_2), .B(in_3[8]), .A(in_4[8]),
    .out_7(n1_bit_alu_8_out_7), .Select_Bits_Op(in_5));
  _1_bit_alu u_1_bit_alu_9 (
    .out_6(out_6[8]), .Cin(n1_bit_alu_8_out_7), .Sub(in_2), .B(in_3[7]), .A(in_4[7]),
    .out_7(n1_bit_alu_9_out_7), .Select_Bits_Op(in_5));
  _1_bit_alu u_1_bit_alu_10 (
    .out_6(out_6[9]), .Cin(n1_bit_alu_9_out_7), .Sub(in_2), .B(in_3[6]), .A(in_4[6]),
    .out_7(n1_bit_alu_10_out_7), .Select_Bits_Op(in_5));
  _1_bit_alu u_1_bit_alu_11 (
    .out_6(out_6[10]), .Cin(n1_bit_alu_10_out_7), .Sub(in_2), .B(in_3[5]), .A(in_4[5]),
    .out_7(n1_bit_alu_11_out_7), .Select_Bits_Op(in_5));
  _1_bit_alu u_1_bit_alu_12 (
    .out_6(out_6[11]), .Cin(n1_bit_alu_11_out_7), .Sub(in_2), .B(in_3[4]), .A(in_4[4]),
    .out_7(n1_bit_alu_12_out_7), .Select_Bits_Op(in_5));
  _1_bit_alu u_1_bit_alu_13 (
    .out_6(out_6[12]), .Cin(n1_bit_alu_12_out_7), .Sub(in_2), .B(in_3[3]), .A(in_4[3]),
    .out_7(n1_bit_alu_13_out_7), .Select_Bits_Op(in_5));
  _1_bit_alu u_1_bit_alu_14 (
    .out_6(out_6[13]), .Cin(n1_bit_alu_13_out_7), .Sub(in_2), .B(in_3[2]), .A(in_4[2]),
    .out_7(n1_bit_alu_14_out_7), .Select_Bits_Op(in_5));
  _1_bit_alu u_1_bit_alu_15 (
    .out_6(out_6[14]), .Cin(n1_bit_alu_14_out_7), .Sub(in_2), .B(in_3[1]), .A(in_4[1]),
    .out_7(n1_bit_alu_15_out_7), .Select_Bits_Op(in_5));
  _1_bit_alu u_1_bit_alu_16 (
    .out_6(out_6[15]), .Cin(n1_bit_alu_15_out_7), .Sub(in_2), .B(in_3[0]), .A(in_4[0]), .out_7(out_7),
    .Select_Bits_Op(in_5));
endmodule

module _1_bit_alu (
  input  Cin,
  input  Sub,
  input  B,
  input  A,
  input  [2:0] Select_Bits_Op,
  output out_6,
  output out_7
);

  wire adder_1_out, and_1_out, comparator_1_eq, comparator_1_gt, comparator_1_lt, multiplier_1_out, or_1_out,
       xor_1_out, xor_2_out;

  xor xor_1 (xor_1_out, B, Sub);
  and and_1 (and_1_out, A, B);
  or or_1 (or_1_out, A, B);
  xor xor_2 (xor_2_out, A, B);
  Adder #(.width(1)) adder_1 (.a(A), .b(xor_1_out), .out(adder_1_out), .cin(Cin), .cout(out_7));
  Multiplier #(.width(1)) multiplier_1 (.a(A), .b(B), .out(multiplier_1_out), .cin(Cin));  // open: cout
  Comparator #(.width(1)) comparator_1 (.a(A), .b(B), .gt(comparator_1_gt), .eq(comparator_1_eq), .lt(comparator_1_lt));
  Multiplexer #(.select(3), .enable("false")) multiplexer_1 (
    .in0(and_1_out), .in1(or_1_out), .in2(xor_2_out), .in3(adder_1_out), .in4(multiplier_1_out),
    .in5(comparator_1_gt), .in6(comparator_1_eq), .in7(comparator_1_lt), .out(out_6), .sel(Select_Bits_Op));
endmodule
