// Logisim project ControlUnit_Implemented.circ as structural Verilog: 5 circuits, main circuit main
module main (
  input  Clear,
  output [15:0] READ_DATA1,
  output [15:0] READ_DATA2,
  output [3:0] OP,
  output [3:0] RS,
  output [3:0] RT,
  output [3:0] RD_Imm,
  output [15:0] Result,
  output AluCout,
  output [2:0] ALUOp,
  output [15:0] Imm
);

  wire Clock_out, controlunit_1_alusrc, controlunit_1_b_cin, controlunit_1_lw, controlunit_1_mem_r,
       controlunit_1_r_d, controlunit_1_r_w, controlunit_1_sw, or_1_out, Reset_out;
  wire [3:0] multiplexer_1_out;
  wire [15:0] adder_1_out, multiplexer_2_out, multiplexer_3_out, PC_q, ram_1_data;

  ControlUnit controlunit_1 (
    .in_1(OP), .R_W(controlunit_1_r_w), .R_D(controlunit_1_r_d), .ALUsrc(controlunit_1_alusrc),
    .ALUop(ALUOp), .LW(controlunit_1_lw), .SW(controlunit_1_sw), .B_Cin(controlunit_1_b_cin),
    .Mem_R(controlunit_1_mem_r));
  Button Reset (.out(Reset_out));
  Register #(.width(16)) PC (.D(adder_1_out), .Q(PC_q), .clk(Clock_out), .clr(Reset_out));  // open: en
  Clock Clock (.out(Clock_out));
  Adder #(.width(16)) adder_1 (.a(PC_q), .b(16'h1), .out(adder_1_out));  // open: cin, cout
  ROM #(.addrWidth(16), .dataWidth(16)) rom_1 (.addr(PC_q), .data({OP, RS, RT, RD_Imm}));  // open: sel
  Multiplexer #(.width(4), .enable("false")) multiplexer_1 (
    .in0(RD_Imm), .in1(RT), .out(multiplexer_1_out), .sel(controlunit_1_r_d));
  assign Imm = {{12{RD_Imm[3]}}, RD_Imm};  // Bit_Extender bit_extender_1
  Register_file register_file_1 (
    .Data(multiplexer_3_out), .CLK(Clock_out), .Register_1_Data(READ_DATA1), .Register_2_Data(READ_DATA2),
    .Write_Register(multiplexer_1_out), .Write_register_2(controlunit_1_r_w), .Read_Register_1(RS),
    .Read_Register_2(RT));
  Multiplexer #(.width(16), .enable("false")) multiplexer_2 (
    .in0(READ_DATA2), .in1(Imm), .out(multiplexer_2_out), .sel(controlunit_1_alusrc));
  _16_bit_ALU u_16_bit_alu_1 (
    .Cin(controlunit_1_b_cin), .Output(Result), .Operand_1(READ_DATA1), .Cout(AluCout), .Operation(ALUOp),
    .Operand_2(multiplexer_2_out), .B_invert(controlunit_1_b_cin));  // open: _0_Flag, Overflow
  or or_1 (or_1_out, controlunit_1_sw, controlunit_1_lw);
  RAM #(.addrWidth(16), .dataWidth(16), .bus("separate")) ram_1 (
    .addr(Result), .din(READ_DATA2), .data(ram_1_data), .str(controlunit_1_sw), .sel(or_1_out),
    .clk(Clock_out), .ld(controlunit_1_lw), .clr(Clear));
  Multiplexer #(.width(16), .enable("false")) multiplexer_3 (
    .in0(Result), .in1(ram_1_data), .out(multiplexer_3_out), .sel(controlunit_1_mem_r));
endmodule

module Register_file (
  input  [3:0] Read_Register_1,
  input  [3:0] Write_Register,
  input  Write_register_2,
  input  [15:0] Data,
  input  CLK,
  input  [3:0] Read_Register_2,
  output [15:0] Register_1_Data,
  output [15:0] Register_2_Data
);

  wire decoder_1_out0, decoder_1_out1, decoder_1_out2, decoder_1_out3, decoder_1_out4, decoder_1_out5,
       decoder_1_out6, decoder_1_out7, decoder_1_out8, decoder_1_out9, decoder_1_out10, decoder_1_out11,
       decoder_1_out12, decoder_1_out13, decoder_1_out14, decoder_1_out15, Reset_out;
  wire [15:0] a0_q, fp_q, gp_q, multiplexer_1_out, ra_q, s0_q, s1_q, s2_q, s3_q, s4_q, s5_q, sp_q, t1_q,
       t2_q, t3_q, to_q, zero_q;

  Decoder #(.select(4)) decoder_1 (
    .out0(decoder_1_out0), .out1(decoder_1_out1), .out2(decoder_1_out2), .out3(decoder_1_out3),
    .out4(decoder_1_out4), .out5(decoder_1_out5), .out6(decoder_1_out6), .out7(decoder_1_out7),
    .out8(decoder_1_out8), .out9(decoder_1_out9), .out10(decoder_1_out10), .out11(decoder_1_out11),
    .out12(decoder_1_out12), .out13(decoder_1_out13), .out14(decoder_1_out14), .out15(decoder_1_out15),
    .sel(Write_Register));  // open: en
  Multiplexer #(.width(16)) multiplexer_1 (
    .in1(Data), .out(multiplexer_1_out), .sel(Write_register_2));  // open: in0, en
  Register #(.width(16)) zero (.D(multiplexer_1_out), .en(decoder_1_out0), .Q(zero_q), .clk(CLK), .clr(Reset_out));
  Register #(.width(16)) to (.D(multiplexer_1_out), .en(decoder_1_out1), .Q(to_q), .clk(CLK), .clr(Reset_out));
  Register #(.width(16)) t1 (.D(multiplexer_1_out), .en(decoder_1_out2), .Q(t1_q), .clk(CLK), .clr(Reset_out));
  Register #(.width(16)) t2 (.D(multiplexer_1_out), .en(decoder_1_out3), .Q(t2_q), .clk(CLK), .clr(Reset_out));
  Register #(.width(16)) t3 (.D(multiplexer_1_out), .en(decoder_1_out4), .Q(t3_q), .clk(CLK), .clr(Reset_out));
  Register #(.width(16)) s0 (.D(multiplexer_1_out), .en(decoder_1_out5), .Q(s0_q), .clk(CLK), .clr(Reset_out));
  Register #(.width(16)) s1 (.D(multiplexer_1_out), .en(decoder_1_out6), .Q(s1_q), .clk(CLK), .clr(Reset_out));
  Register #(.width(16)) s2 (.D(multiplexer_1_out), .en(decoder_1_out7), .Q(s2_q), .clk(CLK), .clr(Reset_out));
  Register #(.width(16)) s3 (.D(multiplexer_1_out), .en(decoder_1_out8), .Q(s3_q), .clk(CLK), .clr(Reset_out));
  Register #(.width(16)) s4 (.D(multiplexer_1_out), .en(decoder_1_out9), .Q(s4_q), .clk(CLK), .clr(Reset_out));
  Register #(.width(16)) s5 (.D(multiplexer_1_out), .en(decoder_1_out10), .Q(s5_q), .clk(CLK), .clr(Reset_out));
  Register #(.width(16)) gp (.D(multiplexer_1_out), .en(decoder_1_out11), .Q(gp_q), .clk(CLK), .clr(Reset_out));
  Register #(.width(16)) sp (.D(multiplexer_1_out), .en(decoder_1_out12), .Q(sp_q), .clk(CLK), .clr(Reset_out));
  Register #(.width(16)) fp (.D(multiplexer_1_out), .en(decoder_1_out13), .Q(fp_q), .clk(CLK), .clr(Reset_out));
  Register #(.width(16)) ra (.D(multiplexer_1_out), .en(decoder_1_out14), .Q(ra_q), .clk(CLK), .clr(Reset_out));
  Register #(.width(16)) a0 (.D(multiplexer_1_out), .en(decoder_1_out15), .Q(a0_q), .clk(CLK), .clr(Reset_out));
  Button Reset (.out(Reset_out));
  Multiplexer #(.select(4), .width(16)) multiplexer_2 (
    .in0(zero_q), .in1(to_q), .in2(t1_q), .in3(t2_q), .in4(t3_q), .in5(s0_q), .in6(s1_q), .in7(s2_q),
    .in8(s3_q), .in9(s4_q), .in10(s5_q), .in11(gp_q), .in12(sp_q), .in13(fp_q), .in14(ra_q), .in15(a0_q),
    .out(Register_1_Data), .sel(Read_Register_1));  // open: en
  Multiplexer #(.select(4), .width(16)) multiplexer_3 (
    .in0(zero_q), .in1(to_q), .in2(t1_q), .in3(t2_q), .in4(t3_q), .in5(s0_q), .in6(s1_q), .in7(s2_q),
    .in8(s3_q), .in9(s4_q), .in10(s5_q), .in11(gp_q), .in12(sp_q), .in13(fp_q), .in14(ra_q), .in15(a0_q),
    .out(Register_2_Data), .sel(Read_Register_2));  // open: en
endmodule

module _1_bit_ALU (
  input  A,
  input  B,
  input  Cin,
  input  [2:0] Operation,
  input  B_invert,
  output Output,
  output Cout
);

  wire adder_1_out, and_1_out, multiplexer_1_out, not_1_out, or_1_out;

  not not_1 (not_1_out, B);
  Multiplexer multiplexer_1 (.in0(B), .in1(not_1_out), .out(multiplexer_1_out), .sel(B_invert));  // open: en
  and and_1 (and_1_out, A, B);
  or or_1 (or_1_out, A, B);
  Adder #(.width(1)) adder_1 (.a(A), .b(multiplexer_1_out), .out(adder_1_out), .cin(Cin), .cout(Cout));
  Multiplexer #(.select(3)) multiplexer_2 (
    .in0(and_1_out), .in1(or_1_out), .in2(adder_1_out), .out(Output), .sel(Operation));  // open: in3, in4, in5, in6, in7, en
endmodule

module _16_bit_ALU (
  input  Cin,
  input  [15:0] Operand_1,
  input  [2:0] Operation,
  input  [15:0] Operand_2,
  input  B_invert,
  output [15:0] Output,
  output _0_Flag,
  output Overflow,
  output Cout
);

  wire n1_bit_alu_1_cout, n1_bit_alu_2_cout, n1_bit_alu_3_cout, n1_bit_alu_4_cout, n1_bit_alu_5_cout,
       n1_bit_alu_6_cout, n1_bit_alu_7_cout, n1_bit_alu_8_cout, n1_bit_alu_9_cout, n1_bit_alu_10_cout,
       n1_bit_alu_11_cout, n1_bit_alu_12_cout, n1_bit_alu_13_cout, n1_bit_alu_14_cout, n1_bit_alu_15_cout;

  _1_bit_ALU u_1_bit_alu_1 (
    .A(Operand_1[0]), .B(Operand_2[0]), .Output(Output[0]), .Cin(Cin), .Operation(Operation),
    .Cout(n1_bit_alu_1_cout), .B_invert(B_invert));
  _1_bit_ALU u_1_bit_alu_2 (
    .A(Operand_1[1]), .B(Operand_2[1]), .Output(Output[1]), .Cin(n1_bit_alu_1_cout), .Operation(Operation),
    .Cout(n1_bit_alu_2_cout), .B_invert(B_invert));
  _1_bit_ALU u_1_bit_alu_3 (
    .A(Operand_1[2]), .B(Operand_2[2]), .Output(Output[2]), .Cin(n1_bit_alu_2_cout), .Operation(Operation),
    .Cout(n1_bit_alu_3_cout), .B_invert(B_invert));
  _1_bit_ALU u_1_bit_alu_4 (
    .A(Operand_1[3]), .B(Operand_2[3]), .Output(Output[3]), .Cin(n1_bit_alu_3_cout), .Operation(Operation),
    .Cout(n1_bit_alu_4_cout), .B_invert(B_invert));
  _1_bit_ALU u_1_bit_alu_5 (
    .A(Operand_1[4]), .B(Operand_2[4]), .Output(Output[4]), .Cin(n1_bit_alu_4_cout), .Operation(Operation),
    .Cout(n1_bit_alu_5_cout), .B_invert(B_invert));
  _1_bit_ALU u_1_bit_alu_6 (
    .A(Operand_1[5]), .B(Operand_2[5]), .Output(Output[5]), .Cin(n1_bit_alu_5_cout), .Operation(Operation),
    .Cout(n1_bit_alu_6_cout), .B_invert(B_invert));
  _1_bit_ALU u_1_bit_alu_7 (
    .A(Operand_1[6]), .B(Operand_2[6]), .Output(Output[6]), .Cin(n1_bit_alu_6_cout), .Operation(Operation),
    .Cout(n1_bit_alu_7_cout), .B_invert(B_invert));
  _1_bit_ALU u_1_bit_alu_8 (
    .A(Operand_1[7]), .B(Operand_2[7]), .Output(Output[7]), .Cin(n1_bit_alu_7_cout), .Operation(Operation),
    .Cout(n1_bit_alu_8_cout), .B_invert(B_invert));
  _1_bit_ALU u_1_bit_alu_9 (
    .A(Operand_1[8]), .B(Operand_2[8]), .Output(Output[8]), .Cin(n1_bit_alu_8_cout), .Operation(Operation),
    .Cout(n1_bit_alu_9_cout), .B_invert(B_invert));
  _1_bit_ALU u_1_bit_alu_10 (
    .A(Operand_1[9]), .B(Operand_2[9]), .Output(Output[9]), .Cin(n1_bit_alu_9_cout), .Operation(Operation),
    .Cout(n1_bit_alu_10_cout), .B_invert(B_invert));
  _1_bit_ALU u_1_bit_alu_11 (
    .A(Operand_1[10]), .B(Operand_2[10]), .Output(Output[10]), .Cin(n1_bit_alu_10_cout),
    .Operation(Operation), .Cout(n1_bit_alu_11_cout), .B_invert(B_invert));
  _1_bit_ALU u_1_bit_alu_12 (
    .A(Operand_1[11]), .B(Operand_2[11]), .Output(Output[11]), .Cin(n1_bit_alu_11_cout),
    .Operation(Operation), .Cout(n1_bit_alu_12_cout), .B_invert(B_invert));
  _1_bit_ALU u_1_bit_alu_13 (
    .A(Operand_1[12]), .B(Operand_2[12]), .Output(Output[12]), .Cin(n1_bit_alu_12_cout),
    .Operation(Operation), .Cout(n1_bit_alu_13_cout), .B_invert(B_invert));
  _1_bit_ALU u_1_bit_alu_14 (
    .A(Operand_1[13]), .B(Operand_2[13]), .Output(Output[13]), .Cin(n1_bit_alu_13_cout),
    .Operation(Operation), .Cout(n1_bit_alu_14_cout), .B_invert(B_invert));
  _1_bit_ALU u_1_bit_alu_15 (
    .A(Operand_1[14]), .B(Operand_2[14]), .Output(Output[14]), .Cin(n1_bit_alu_14_cout),
    .Operation(Operation), .Cout(n1_bit_alu_15_cout), .B_invert(B_invert));
  _1_bit_ALU u_1_bit_alu_16 (
    .A(Operand_1[15]), .B(Operand_2[15]), .Output(Output[15]), .Cin(n1_bit_alu_15_cout),
    .Operation(Operation), .Cout(Cout), .B_invert(B_invert));
  xor xor_1 (Overflow, n1_bit_alu_15_cout, Cout);
  nor nor_1 (_0_Flag, Output[0], Output[1], Output[2], Output[3], Output[4], Output[5], Output[6], Output[7], Output[8], Output[9], Output[10], Output[11], Output[12], Output[13], Output[14], Output[15]);
endmodule

module ControlUnit (
  input  [3:0] in_1,
  output R_W,
  output R_D,
  output ALUsrc,
  output [2:0] ALUop,
  output LW,
  output SW,
  output B_Cin,
  output Mem_R
);

  wire and_1_out, and_2_out, and_3_out, and_4_out, and_5_out, and_6_out, and_7_out, and_8_out, and_9_out,
       and_10_out, and_11_out, and_12_out, and_13_out, and_14_out, and_15_out, and_16_out, and_17_out,
       and_18_out, and_19_out, and_20_out, and_23_out, and_24_out, and_25_out, and_26_out, not_1_out,
       not_2_out, not_3_out, not_4_out, not_5_out, not_6_out, not_7_out, not_8_out, not_9_out, not_10_out,
       not_11_out, not_12_out, not_13_out, not_14_out, not_15_out, not_16_out, not_17_out, not_18_out,
       not_19_out, not_20_out, not_21_out, not_22_out, not_23_out, not_24_out, not_25_out, not_26_out,
       not_27_out, not_28_out, not_29_out, not_30_out, not_31_out, not_32_out, not_33_out, not_34_out,
       not_35_out, not_36_out, not_37_out, not_38_out, not_39_out, not_40_out, not_41_out, not_42_out,
       not_43_out, not_44_out, not_45_out, not_46_out, not_47_out, not_48_out, not_49_out, not_50_out,
       not_51_out;

  not not_1 (not_1_out, in_1[0]);
  not not_2 (not_2_out, in_1[1]);
  not not_3 (not_3_out, in_1[2]);
  not not_4 (not_4_out, in_1[3]);
  not not_5 (not_5_out, in_1[1]);
  not not_6 (not_6_out, in_1[0]);
  not not_7 (not_7_out, in_1[0]);
  not not_8 (not_8_out, in_1[1]);
  not not_9 (not_9_out, in_1[0]);
  not not_10 (not_10_out, in_1[0]);
  not not_11 (not_11_out, not_6_out);
  not not_12 (not_12_out, in_1[2]);
  not not_13 (not_13_out, in_1[3]);
  not not_14 (not_14_out, in_1[2]);
  not not_15 (not_15_out, not_9_out);
  not not_16 (not_16_out, in_1[1]);
  not not_17 (not_17_out, in_1[2]);
  not not_18 (not_18_out, in_1[3]);
  not not_19 (not_19_out, not_9_out);
  not not_20 (not_20_out, not_8_out);
  not not_21 (not_21_out, in_1[3]);
  not not_22 (not_22_out, not_5_out);
  not not_23 (not_23_out, in_1[2]);
  not not_24 (not_24_out, in_1[2]);
  not not_25 (not_25_out, in_1[3]);
  not not_26 (not_26_out, in_1[0]);
  not not_27 (not_27_out, in_1[1]);
  not not_28 (not_28_out, not_6_out);
  not not_29 (not_29_out, in_1[1]);
  not not_30 (not_30_out, in_1[2]);
  not not_31 (not_31_out, not_13_out);
  not not_32 (not_32_out, in_1[0]);
  not not_33 (not_33_out, in_1[1]);
  not not_34 (not_34_out, in_1[2]);
  not not_35 (not_35_out, in_1[3]);
  and and_1 (and_1_out, in_1[0], in_1[2], not_4_out);
  and and_2 (and_2_out, in_1[0], in_1[1], in_1[2], in_1[3]);
  not not_36 (not_36_out, in_1[0]);
  and and_3 (and_3_out, not_36_out, not_8_out, not_37_out, in_1[3]);
  not not_37 (not_37_out, not_14_out);
  and and_4 (and_4_out, not_15_out, not_16_out, not_17_out, not_18_out);
  and and_5 (and_5_out, not_19_out, not_20_out, not_38_out, not_21_out);
  not not_38 (not_38_out, not_14_out);
  and and_6 (and_6_out, not_10_out, not_22_out, not_23_out, not_39_out);
  not not_39 (not_39_out, in_1[3]);
  not not_40 (not_40_out, not_5_out);
  and and_7 (and_7_out, not_11_out, not_40_out, not_24_out, not_25_out);
  and and_8 (and_8_out, not_26_out, not_27_out, not_41_out, not_42_out);
  not not_41 (not_41_out, not_12_out);
  not not_42 (not_42_out, in_1[3]);
  not not_43 (not_43_out, not_6_out);
  not not_44 (not_44_out, in_1[1]);
  and and_9 (and_9_out, not_43_out, not_44_out, not_45_out, not_46_out);
  not not_45 (not_45_out, not_12_out);
  not not_46 (not_46_out, in_1[3]);
  not not_47 (not_47_out, in_1[0]);
  not not_48 (not_48_out, in_1[1]);
  and and_10 (and_10_out, not_47_out, not_48_out, not_49_out, not_50_out);
  not not_49 (not_49_out, in_1[2]);
  not not_50 (not_50_out, not_13_out);
  and and_11 (and_11_out, not_28_out, not_29_out, not_30_out, not_31_out);
  and and_12 (and_12_out, not_1_out, not_2_out, not_3_out, not_4_out);
  and and_13 (and_13_out, in_1[0], not_2_out, not_3_out, not_4_out);
  and and_14 (and_14_out, not_1_out, in_1[1], not_3_out, not_4_out);
  and and_15 (and_15_out, in_1[0], in_1[1], not_3_out, not_4_out);
  and and_16 (and_16_out, not_1_out, not_2_out, in_1[2], not_4_out);
  and and_17 (and_17_out, not_7_out, in_1[1], in_1[2], not_4_out);
  and and_18 (and_18_out, in_1[0], in_1[1], in_1[2], not_4_out);
  and and_19 (and_19_out, not_2_out, not_2_out, not_3_out, in_1[3]);
  and and_20 (and_20_out, in_1[0], not_2_out, not_3_out, in_1[3]);
  not not_51 (not_51_out, not_34_out);
  or _010 (ALUop[2], and_2_out, and_3_out);
  or _000 (ALUop[0], and_4_out, and_5_out);
  or _001 (ALUop[1], and_6_out, and_7_out, and_8_out, and_9_out, and_10_out, and_11_out);
  and and_21 (LW, not_32_out, not_33_out, not_51_out, not_35_out);
  and and_22 (SW, in_1[0], not_33_out, in_1[2], not_35_out);
  and and_23 (and_23_out, in_1[0], in_1[1], not_34_out, not_35_out);
  and and_24 (and_24_out, in_1[0], not_33_out, not_34_out, in_1[3]);
  and and_25 (and_25_out, not_32_out, not_33_out, in_1[2], not_35_out);
  and and_26 (and_26_out, in_1[0], not_33_out, in_1[2], not_35_out);
  or or_1 (R_W, and_12_out, and_13_out, and_14_out, and_15_out, and_16_out, and_17_out, and_18_out, and_19_out, and_20_out);
  or or_2 (ALUsrc, and_16_out, and_1_out, and_17_out, and_18_out, and_19_out, and_20_out);
  or or_3 (B_Cin, and_23_out, and_24_out);
  or or_4 (Mem_R, and_25_out, and_26_out);

  assign R_D = ALUsrc;
endmodule
