// Logisim project Lab 3.circ as structural Verilog
module Mul_4x4 (
  input  B4,
  input  B3,
  input  B2,
  input  B1,
  input  A4,
  input  A3,
  input  A2,
  input  A1,
  output S8,
  output S7,
  output S6,
  output S5,
  output S4,
  output S3,
  output S2,
  output S1
);

  wire [2:0] and_15_out;
  wire [3:0] adder_2_cout, adder_3_cout, and_5_out, and_8_out, and_11_out;

  and and_1 (and_5_out[2], A4, B3);
  and and_2 (and_5_out[3], A4, B4);
  and and_3 (and_5_out[1], A4, B2);
  and and_4 (and_8_out[3], A3, B4);
  and and_5 (and_5_out[0], A4, B1);
  and and_6 (and_8_out[1], A3, B2);
  and and_7 (and_8_out[2], A3, B3);
  and and_8 (and_8_out[0], A3, B1);
  and and_9 (and_11_out[3], A2, B4);
  and and_10 (and_11_out[2], A2, B3);
  Adder #(.width(4)) adder_1 (.a(adder_2_cout), .b(and_5_out), .out({S7, S6, S5, S4}), .cout(S8));  // open: cin
  and and_11 (and_11_out[0], A2, B1);
  and and_12 (and_11_out[1], A2, B2);
  Adder #(.width(4)) adder_2 (
    .a(adder_3_cout), .b(and_8_out), .out({adder_2_cout[2:0], S3}), .cout(adder_2_cout[3]));  // open: cin
  and and_13 (and_15_out[2], A1, B4);
  and and_14 (and_15_out[1], A1, B3);
  and and_15 (and_15_out[0], A1, B2);
  Adder #(.width(4)) adder_3 (
    .a({1'b0, and_15_out}), .b(and_11_out), .out({adder_3_cout[2:0], S2}), .cout(adder_3_cout[3]));  // open: cin
  and and_16 (S1, A1, B1);
endmodule

module mul2X2 (
  input  A1,
  input  A2,
  input  B1,
  input  B2,
  output S1,
  output S2,
  output S3,
  output S4
);

  wire and_1_out, and_3_out, and_4_out, and_5_out;

  and and_1 (and_1_out, A1, B2);
  and and_2 (S1, A1, B1);
  and and_3 (and_3_out, A2, B1);
  and and_4 (and_4_out, A2, B2);
  xor xor_1 (S2, and_1_out, and_3_out);
  and and_5 (and_5_out, and_1_out, and_3_out);
  xor xor_2 (S3, and_4_out, and_5_out);
  and and_6 (S4, and_5_out, and_4_out);
endmodule
