// Logisim project Register File(2 bit).circ as structural Verilog: 2 circuits, main circuit main
// CPU
module main (
  input  [1:0] RS,
  input  [1:0] RT,
  input  [1:0] RD,
  input  [1:0] Write_Data_in_RD,
  output [1:0] Read_Data_from_RS,
  output [1:0] Read_Data_from_RT
);

  wire Clock_out;

  Clock Clock (.out(Clock_out));
  Register_File register_file_1 (
    .Data_IN(Write_Data_in_RD), .Data01(Read_Data_from_RS), .Data02(Read_Data_from_RT), .Data_Address(RD),
    .clk(Clock_out), .RS(RS), .RT(RT));
endmodule

module Register_File (
  input  [1:0] Data_IN,
  input  [1:0] Data_Address,
  input  [1:0] RS,
  input  clk,
  input  [1:0] RT,
  output [1:0] Data01,
  output [1:0] Data02
);

  wire decoder_1_out0, decoder_1_out1, decoder_1_out2, decoder_1_out3;
  wire [1:0] register_1_q, register_2_q, register_3_q, register_4_q;

  Decoder #(.select(2)) decoder_1 (
    .out0(decoder_1_out0), .out1(decoder_1_out1), .out2(decoder_1_out2), .out3(decoder_1_out3),
    .sel(Data_Address));  // open: en
  Register #(.width(2)) register_1 (.D(Data_IN), .en(decoder_1_out0), .Q(register_1_q), .clk(clk));  // open: clr
  Register #(.width(2)) register_2 (.D(Data_IN), .en(decoder_1_out1), .Q(register_2_q), .clk(clk));  // open: clr
  Register #(.width(2)) register_3 (.D(Data_IN), .en(decoder_1_out2), .Q(register_3_q), .clk(clk));  // open: clr
  Register #(.width(2)) register_4 (.D(Data_IN), .en(decoder_1_out3), .Q(register_4_q), .clk(clk));  // open: clr
  Multiplexer #(.select(2), .width(2)) multiplexer_1 (
    .in0(register_1_q), .in1(register_2_q), .in2(register_3_q), .in3(register_4_q), .out(Data01), .sel(RS));  // open: en
  Multiplexer #(.select(2), .width(2)) multiplexer_2 (
    .in0(register_1_q), .in1(register_2_q), .in2(register_3_q), .in3(register_4_q), .out(Data02), .sel(RT));  // open: en
endmodule
