// Logisim project Up_down_counter.circ as structural Verilog: 2 circuits, main circuit main
module main (
);

  counter counter_1 ();  // open: Up, Down, A, B, C, D
  counter counter_2 ();  // open: Up, Down, A, B, C, D
endmodule

module counter (
  input  Up,
  input  Down,
  output C,
  output D,
  output A,
  output B
);

  wire and_1_out, and_2_out, and_3_out, and_4_out, and_5_out, and_6_out, and_7_out, Clock_out, d_ff_1_qn,
       d_ff_2_qn, d_ff_3_qn, not_1_out, or_1_out, or_2_out, or_3_out, or_4_out, RESET_out, xor_1_out,
       xor_2_out, xor_3_out, xor_4_out;

  not not_1 (not_1_out, Up);
  and and_1 (and_1_out, not_1_out, Down);
  and and_2 (and_2_out, and_1_out, d_ff_1_qn);
  and and_3 (and_3_out, and_2_out, d_ff_2_qn);
  and and_4 (and_4_out, Up, D);
  and and_5 (and_5_out, and_4_out, C);
  and and_6 (and_6_out, and_3_out, d_ff_3_qn);
  and and_7 (and_7_out, and_5_out, B);
  or or_1 (or_1_out, Up, and_1_out);
  or or_2 (or_2_out, and_4_out, and_2_out);
  or or_3 (or_3_out, and_5_out, and_3_out);
  or or_4 (or_4_out, and_7_out, and_6_out);
  xor xor_1 (xor_1_out, D, or_1_out);
  xor xor_2 (xor_2_out, C, or_2_out);
  xor xor_3 (xor_3_out, B, or_3_out);
  xor xor_4 (xor_4_out, A, or_4_out);
  Clock Clock (.out(Clock_out));
  Button RESET (.out(RESET_out));
  D_Flip_Flop d_ff_1 (.clk(Clock_out), .D(xor_1_out), .Q(D), .Qn(d_ff_1_qn), .reset(RESET_out));  // open: preset, en
  D_Flip_Flop d_ff_2 (.clk(Clock_out), .D(xor_2_out), .Q(C), .Qn(d_ff_2_qn), .reset(RESET_out));  // open: preset, en
  D_Flip_Flop d_ff_3 (.clk(Clock_out), .D(xor_3_out), .Q(B), .Qn(d_ff_3_qn), .reset(RESET_out));  // open: preset, en
  D_Flip_Flop d_ff_4 (.clk(Clock_out), .D(xor_4_out), .Q(A), .reset(RESET_out));  // open: Qn, preset, en

  // Notes on the sheet:
  //   4 BIT BINARY UP -Down Counter
endmodule
