// Logisim project pipeline.circ as structural Verilog: 5 circuits, main circuit main
// CPU
module main (
  input  in_1,
  input  R_I,
  input  R_W,
  input  R__I_Type,
  input  Sw,
  input  sl,
  input  lw,
  input  Clear,
  input  mem_alu_R,
  output [3:0] Opcode,
  output [3:0] RS,
  output [15:0] Read_Data_1,
  output [3:0] RT,
  output [3:0] RD_Imm,
  output [15:0] Read_Data_2,
  output [15:0] out_16,
  output [15:0] out_17,
  output [15:0] out_18,
  output [1:0] ALU_Op
);

  wire clock_1_out;
  wire [3:0] multiplexer_1_out;
  wire [15:0] adder_1_out, multiplexer_2_out, ram_1_data, register_1_q;

  Register #(.width(16)) register_1 (.D(adder_1_out), .Q(register_1_q), .clk(clock_1_out));  // open: en, clr
  Clock clock_1 (.out(clock_1_out));
  Adder #(.width(16)) adder_1 (.a(register_1_q), .b(16'h1), .out(adder_1_out));  // open: cin, cout
  ROM #(.addrWidth(16), .dataWidth(16)) rom_1 (.addr(register_1_q), .data({Opcode, RS, RT, RD_Imm}));  // open: sel
  Multiplexer #(.width(4), .enable("false")) multiplexer_1 (.in0(RD_Imm), .in1(RT), .out(multiplexer_1_out), .sel(R_I));
  assign out_18 = {{12{1'b0}}, multiplexer_1_out};  // Bit_Extender bit_extender_1
  Register_File register_file_1 (
    .Data_IN(out_17), .Data01(Read_Data_1), .Data02(Read_Data_2), .Data_Address(multiplexer_1_out), .RS(RS),
    .RT(RT), .in_2(R_W), .in_5(clock_1_out));
  Bit_Extender #(.in_width(4), .out_width(2)) bit_extender_2 (.in(Opcode), .out(ALU_Op));
  Multiplexer #(.width(16), .enable("false")) multiplexer_2 (
    .in0(Read_Data_2), .in1(out_18), .out(multiplexer_2_out), .sel(R__I_Type));
  ALU_16_bit alu_16_bit_1 (
    .A(Read_Data_1), .B(multiplexer_2_out), .Opcode(ALU_Op), .Carry_In(in_1), .Result(out_16));  // open: Overflow, Carry_Out, Zero_Signal
  Multiplexer #(.width(16), .enable("false")) multiplexer_3 (
    .in0(out_16), .in1(ram_1_data), .out(out_17), .sel(mem_alu_R));
  RAM #(.addrWidth(16), .dataWidth(16), .bus("separate")) ram_1 (
    .addr(out_16), .din(Read_Data_2), .data(ram_1_data), .str(Sw), .sel(sl), .clk(clock_1_out), .ld(lw),
    .clr(Clear));

  // Notes on the sheet:
  //   contents of rom_1 (hex, n*v repeats v):
  //   2231
endmodule

module Register_File (
  input  [15:0] Data_IN,
  input  in_2,
  input  [3:0] Data_Address,
  input  [3:0] RS,
  input  in_5,
  input  [3:0] RT,
  output [15:0] Data01,
  output [15:0] Data02
);

  wire demultiplexer_1_out0, demultiplexer_1_out1, demultiplexer_1_out2, demultiplexer_1_out3,
       demultiplexer_1_out4, demultiplexer_1_out5, demultiplexer_1_out6, demultiplexer_1_out7,
       demultiplexer_1_out8, demultiplexer_1_out9, demultiplexer_1_out10, demultiplexer_1_out11,
       demultiplexer_1_out12, demultiplexer_1_out13, demultiplexer_1_out14, demultiplexer_1_out15;
  wire [15:0] register_1_q, register_2_q, register_3_q, register_4_q, register_5_q, register_6_q,
       register_7_q, register_8_q, register_9_q, register_10_q, register_11_q, register_12_q, register_13_q,
       register_14_q, register_15_q, register_16_q;

  Demultiplexer #(.select(4)) demultiplexer_1 (
    .out0(demultiplexer_1_out0), .out1(demultiplexer_1_out1), .out2(demultiplexer_1_out2),
    .out3(demultiplexer_1_out3), .out4(demultiplexer_1_out4), .out5(demultiplexer_1_out5),
    .out6(demultiplexer_1_out6), .out7(demultiplexer_1_out7), .out8(demultiplexer_1_out8),
    .out9(demultiplexer_1_out9), .out10(demultiplexer_1_out10), .out11(demultiplexer_1_out11),
    .out12(demultiplexer_1_out12), .out13(demultiplexer_1_out13), .out14(demultiplexer_1_out14),
    .out15(demultiplexer_1_out15), .in(in_2), .sel(Data_Address));  // open: en
  Register #(.width(16)) register_1 (
    .D(Data_IN), .en(demultiplexer_1_out0), .Q(register_1_q), .clk(in_5));  // open: clr
  Register #(.width(16)) register_2 (
    .D(Data_IN), .en(demultiplexer_1_out1), .Q(register_2_q), .clk(in_5));  // open: clr
  Register #(.width(16)) register_3 (
    .D(Data_IN), .en(demultiplexer_1_out2), .Q(register_3_q), .clk(in_5));  // open: clr
  Register #(.width(16)) register_4 (
    .D(Data_IN), .en(demultiplexer_1_out3), .Q(register_4_q), .clk(in_5));  // open: clr
  Register #(.width(16)) register_5 (
    .D(Data_IN), .en(demultiplexer_1_out4), .Q(register_5_q), .clk(in_5));  // open: clr
  Register #(.width(16)) register_6 (
    .D(Data_IN), .en(demultiplexer_1_out5), .Q(register_6_q), .clk(in_5));  // open: clr
  Register #(.width(16)) register_7 (
    .D(Data_IN), .en(demultiplexer_1_out6), .Q(register_7_q), .clk(in_5));  // open: clr
  Register #(.width(16)) register_8 (
    .D(Data_IN), .en(demultiplexer_1_out7), .Q(register_8_q), .clk(in_5));  // open: clr
  Register #(.width(16)) register_9 (
    .D(Data_IN), .en(demultiplexer_1_out8), .Q(register_9_q), .clk(in_5));  // open: clr
  Register #(.width(16)) register_10 (
    .D(Data_IN), .en(demultiplexer_1_out9), .Q(register_10_q), .clk(in_5));  // open: clr
  Register #(.width(16)) register_11 (
    .D(Data_IN), .en(demultiplexer_1_out10), .Q(register_11_q), .clk(in_5));  // open: clr
  Register #(.width(16)) register_12 (
    .D(Data_IN), .en(demultiplexer_1_out11), .Q(register_12_q), .clk(in_5));  // open: clr
  Register #(.width(16)) register_13 (
    .D(Data_IN), .en(demultiplexer_1_out12), .Q(register_13_q), .clk(in_5));  // open: clr
  Register #(.width(16)) register_14 (
    .D(Data_IN), .en(demultiplexer_1_out13), .Q(register_14_q), .clk(in_5));  // open: clr
  Register #(.width(16)) register_15 (
    .D(Data_IN), .en(demultiplexer_1_out14), .Q(register_15_q), .clk(in_5));  // open: clr
  Register #(.width(16)) register_16 (
    .D(Data_IN), .en(demultiplexer_1_out15), .Q(register_16_q), .clk(in_5));  // open: clr
  Multiplexer #(.select(4), .width(16)) multiplexer_1 (
    .in0(register_1_q), .in1(register_2_q), .in2(register_3_q), .in3(register_4_q), .in4(register_5_q),
    .in5(register_6_q), .in6(register_7_q), .in7(register_8_q), .in8(register_9_q), .in9(register_10_q),
    .in10(register_11_q), .in11(register_12_q), .in12(register_13_q), .in13(register_14_q),
    .in14(register_15_q), .in15(register_16_q), .out(Data01), .sel(RS));  // open: en
  Multiplexer #(.select(4), .width(16)) multiplexer_2 (
    .in0(register_1_q), .in1(register_2_q), .in2(register_3_q), .in3(register_4_q), .in4(register_5_q),
    .in5(register_6_q), .in6(register_7_q), .in7(register_8_q), .in8(register_9_q), .in9(register_10_q),
    .in10(register_11_q), .in11(register_12_q), .in12(register_13_q), .in13(register_14_q),
    .in14(register_15_q), .in15(register_16_q), .out(Data02), .sel(RT));  // open: en
endmodule

module ALU_1_bit (
  input  A,
  input  B,
  input  C_in,
  input  [1:0] ALU_Opcode,
  output Result,
  output Overflow,
  output Zero_Signal,
  output C_out
);

  wire adder_1_out, and_1_out, or_1_out, subtractor_1_out;

  and and_1 (and_1_out, A, B);
  or or_1 (or_1_out, A, B);
  Adder #(.width(1)) adder_1 (.a(A), .b(B), .out(adder_1_out), .cin(C_in), .cout(C_out));
  Subtractor #(.width(1)) subtractor_1 (.a(A), .b(B), .out(subtractor_1_out));  // open: bin, bout
  Multiplexer #(.select(2), .enable("false")) multiplexer_1 (
    .in0(and_1_out), .in1(or_1_out), .in2(adder_1_out), .in3(subtractor_1_out), .out(Result), .sel(ALU_Opcode));
  xor xor_1 (Overflow, Result, C_out);
  nor nor_1 (Zero_Signal, Result, C_out);
endmodule

module ALU_16_bit (
  input  [1:0] Opcode,
  input  Carry_In,
  input  [15:0] A,
  input  [15:0] B,
  output Carry_Out,
  output [15:0] Result,
  output [15:0] Overflow,
  output [15:0] Zero_Signal
);

  wire alu_1_bit_1_c_out, alu_1_bit_2_c_out, alu_1_bit_3_c_out, alu_1_bit_4_c_out, alu_1_bit_5_c_out,
       alu_1_bit_6_c_out, alu_1_bit_7_c_out, alu_1_bit_8_c_out, alu_1_bit_9_c_out, alu_1_bit_10_c_out,
       alu_1_bit_11_c_out, alu_1_bit_12_c_out, alu_1_bit_13_c_out, alu_1_bit_14_c_out, alu_1_bit_15_c_out;

  ALU_1_bit alu_1_bit_1 (
    .Result(Result[0]), .Overflow(Overflow[15]), .Zero_Signal(Zero_Signal[0]), .C_out(alu_1_bit_1_c_out),
    .A(B[0]), .B(A[0]), .C_in(Carry_In), .ALU_Opcode(Opcode));
  ALU_1_bit alu_1_bit_2 (
    .Result(Result[1]), .Overflow(Overflow[14]), .Zero_Signal(Zero_Signal[1]), .C_out(alu_1_bit_2_c_out),
    .A(B[1]), .B(A[1]), .C_in(alu_1_bit_1_c_out), .ALU_Opcode(Opcode));
  ALU_1_bit alu_1_bit_3 (
    .Result(Result[2]), .Overflow(Overflow[13]), .Zero_Signal(Zero_Signal[2]), .C_out(alu_1_bit_3_c_out),
    .A(B[2]), .B(A[2]), .C_in(alu_1_bit_2_c_out), .ALU_Opcode(Opcode));
  ALU_1_bit alu_1_bit_4 (
    .Result(Result[3]), .Overflow(Overflow[12]), .Zero_Signal(Zero_Signal[3]), .C_out(alu_1_bit_4_c_out),
    .A(B[3]), .B(A[3]), .C_in(alu_1_bit_3_c_out), .ALU_Opcode(Opcode));
  ALU_1_bit alu_1_bit_5 (
    .Result(Result[4]), .Overflow(Overflow[11]), .Zero_Signal(Zero_Signal[4]), .C_out(alu_1_bit_5_c_out),
    .A(B[4]), .B(A[4]), .C_in(alu_1_bit_4_c_out), .ALU_Opcode(Opcode));
  ALU_1_bit alu_1_bit_6 (
    .Result(Result[5]), .Overflow(Overflow[10]), .Zero_Signal(Zero_Signal[5]), .C_out(alu_1_bit_6_c_out),
    .A(B[5]), .B(A[5]), .C_in(alu_1_bit_5_c_out), .ALU_Opcode(Opcode));
  ALU_1_bit alu_1_bit_7 (
    .Result(Result[6]), .Overflow(Overflow[9]), .Zero_Signal(Zero_Signal[6]), .C_out(alu_1_bit_7_c_out),
    .A(B[6]), .B(A[6]), .C_in(alu_1_bit_6_c_out), .ALU_Opcode(Opcode));
  ALU_1_bit alu_1_bit_8 (
    .Result(Result[7]), .Overflow(Overflow[8]), .Zero_Signal(Zero_Signal[7]), .C_out(alu_1_bit_8_c_out),
    .A(B[7]), .B(A[7]), .C_in(alu_1_bit_7_c_out), .ALU_Opcode(Opcode));
  ALU_1_bit alu_1_bit_9 (
    .Result(Result[8]), .Overflow(Overflow[7]), .Zero_Signal(Zero_Signal[8]), .C_out(alu_1_bit_9_c_out),
    .A(B[8]), .B(A[8]), .C_in(alu_1_bit_8_c_out), .ALU_Opcode(Opcode));
  ALU_1_bit alu_1_bit_10 (
    .Result(Result[9]), .Overflow(Overflow[6]), .Zero_Signal(Zero_Signal[9]), .C_out(alu_1_bit_10_c_out),
    .A(B[9]), .B(A[9]), .C_in(alu_1_bit_9_c_out), .ALU_Opcode(Opcode));
  ALU_1_bit alu_1_bit_11 (
    .Result(Result[10]), .Overflow(Overflow[5]), .Zero_Signal(Zero_Signal[10]), .C_out(alu_1_bit_11_c_out),
    .A(B[10]), .B(A[10]), .C_in(alu_1_bit_10_c_out), .ALU_Opcode(Opcode));
  ALU_1_bit alu_1_bit_12 (
    .Result(Result[11]), .Overflow(Overflow[4]), .Zero_Signal(Zero_Signal[11]), .C_out(alu_1_bit_12_c_out),
    .A(B[11]), .B(A[11]), .C_in(alu_1_bit_11_c_out), .ALU_Opcode(Opcode));
  ALU_1_bit alu_1_bit_13 (
    .Result(Result[12]), .Overflow(Overflow[3]), .Zero_Signal(Zero_Signal[12]), .C_out(alu_1_bit_13_c_out),
    .A(B[12]), .B(A[12]), .C_in(alu_1_bit_12_c_out), .ALU_Opcode(Opcode));
  ALU_1_bit alu_1_bit_14 (
    .Result(Result[13]), .Overflow(Overflow[2]), .Zero_Signal(Zero_Signal[13]), .C_out(alu_1_bit_14_c_out),
    .A(B[13]), .B(A[13]), .C_in(alu_1_bit_13_c_out), .ALU_Opcode(Opcode));
  ALU_1_bit alu_1_bit_15 (
    .Result(Result[14]), .Overflow(Overflow[1]), .Zero_Signal(Zero_Signal[14]), .C_out(alu_1_bit_15_c_out),
    .A(B[14]), .B(A[14]), .C_in(alu_1_bit_14_c_out), .ALU_Opcode(Opcode));
  ALU_1_bit alu_1_bit_16 (
    .Result(Result[15]), .Overflow(Overflow[0]), .Zero_Signal(Zero_Signal[15]), .C_out(Carry_Out), .A(B[15]),
    .B(A[15]), .C_in(alu_1_bit_15_c_out), .ALU_Opcode(Opcode));
endmodule

module pipeline (
  input  in_1,
  input  Clear,
  input  in_3,
  input  in_4,
  input  in_5,
  input  [1:0] in_6,
  input  in_7,
  input  in_8,
  input  in_9,
  input  in_10,
  output [3:0] Opcode,
  output [3:0] RS,
  output [15:0] Read_Data_1,
  output [3:0] RT,
  output [3:0] RD_Imm,
  output [15:0] Read_Data_2,
  output [15:0] out_17,
  output [15:0] out_18,
  output [1:0] ALU_Op,
  output [3:0] RD,
  output [3:0] RD_2
);

  wire clock_1_out;
  wire [3:0] multiplexer_1_out, register_13_q;
  wire [15:0] adder_1_out, alu_16_bit_1_result, bit_extender_1_out, multiplexer_2_out, ram_1_data,
       register_1_q, register_2_q, register_4_q, register_6_q, register_7_q, register_8_q, register_11_q,
       register_12_q, rom_1_data;

  Register #(.width(16)) register_1 (.D(register_2_q), .Q(register_1_q), .clk(clock_1_out), .clr(in_1));  // open: en
  Adder #(.width(16)) adder_1 (.a(register_1_q), .b(16'h1), .out(adder_1_out));  // open: cin, cout
  ROM #(.addrWidth(16), .dataWidth(16)) rom_1 (.addr(register_1_q), .data(rom_1_data));  // open: sel
  Clock clock_1 (.out(clock_1_out));
  Register #(.width(16)) register_2 (.D(adder_1_out), .Q(register_2_q), .clk(clock_1_out), .clr(in_1));  // open: en
  Register #(.width(16)) register_3 (
    .D(rom_1_data), .Q({Opcode, RS, RT, RD_Imm}), .clk(clock_1_out), .clr(in_1));  // open: en
  Multiplexer #(.width(4), .enable("false")) multiplexer_1 (
    .in0(RD_Imm), .in1(RT), .out(multiplexer_1_out), .sel(in_4));
  assign bit_extender_1_out = {{12{1'b0}}, RD_Imm};  // Bit_Extender bit_extender_1
  Register_File register_file_1 (
    .Data_IN(out_18), .Data01(Read_Data_1), .Data02(Read_Data_2), .Data_Address(register_13_q), .RS(RS),
    .RT(RT), .in_2(in_3), .in_5(clock_1_out));
  Register #(.width(16)) register_4 (
    .D(bit_extender_1_out), .Q(register_4_q), .clk(clock_1_out), .clr(in_1));  // open: en
  Register #(.width(4)) register_5 (.D(multiplexer_1_out), .Q(RD), .clk(clock_1_out), .clr(in_1));  // open: en
  Multiplexer #(.width(16), .enable("false")) multiplexer_2 (
    .in0(Read_Data_2), .in1(register_4_q), .out(multiplexer_2_out), .sel(in_5));
  Register #(.width(16)) register_6 (.D(Read_Data_1), .Q(register_6_q), .clk(clock_1_out), .clr(in_1));  // open: en
  Register #(.width(16)) register_7 (
    .D(multiplexer_2_out), .Q(register_7_q), .clk(clock_1_out), .clr(in_1));  // open: en
  Register #(.width(16)) register_8 (.D(Read_Data_2), .Q(register_8_q), .clk(clock_1_out), .clr(in_1));  // open: en
  Register #(.width(16)) register_9 (.D(alu_16_bit_1_result), .Q(out_17), .clk(clock_1_out), .clr(in_1));  // open: en
  ALU_16_bit alu_16_bit_1 (
    .A(register_6_q), .B(register_7_q), .Opcode(in_6), .Result(alu_16_bit_1_result));  // open: Carry_In, Overflow, Carry_Out, Zero_Signal
  Register #(.width(4)) register_10 (.D(RD), .Q(RD_2), .clk(clock_1_out), .clr(in_1));  // open: en
  RAM #(.addrWidth(16), .dataWidth(16), .bus("separate")) ram_1 (
    .addr(out_17), .din(register_8_q), .data(ram_1_data), .str(in_8), .sel(in_9), .clk(clock_1_out),
    .ld(in_7), .clr(Clear));
  Register #(.width(16)) register_11 (.D(out_17), .Q(register_11_q), .clk(clock_1_out), .clr(in_1));  // open: en
  Register #(.width(16)) register_12 (.D(ram_1_data), .Q(register_12_q), .clk(clock_1_out), .clr(in_1));  // open: en
  Register #(.width(4)) register_13 (.D(RD_2), .Q(register_13_q), .clk(clock_1_out), .clr(in_1));  // open: en
  Multiplexer #(.width(16), .enable("false")) multiplexer_3 (
    .in0(register_12_q), .in1(register_11_q), .out(out_18), .sel(in_10));

  assign ALU_Op = in_6;

  // Other names for the same wires on the sheet: lw = in_7; Mem_Res = in_10; R_D = in_4; R_I = in_5; R_W = in_3;
  //   sl = in_9; sw = in_8
endmodule
